# Fritzing sketch Plaque-Induction-domotique (saved by Fritzing 1.0.2b)
breadboards: 1

parts:
  RY1 = SSR-40VA
  L1 = sct-013 [part_number=sct-013 package="4Ucon 08780 [THT]"]
  S1 = Pushbutton [package="[THT]"]
  R1 = Resistor [tolerance=±5% power=0.25 resistance=10k package=THT]
  R2 = Resistor [tolerance=±5% power=0.25 resistance=10k package=THT]
  A2 = Arduino MKR Wifi 1010
  C1 = Electrolytic Capacitor [capacitance=1µF voltage=35V package="100 mil [THT, electrolytic]"]

nets:
  N1: RY1.Pin_3, A2.~D5
  N2: RY1.Pin_4, R1.Pin_1, A2.VIN, C1.-
  N3: L1.pin_0, R1.Pin_0, R2.Pin_1, C1.+
  N4: L1.pin_1, A2.A1
  N5: S1.Pin_1, S1.Pin_2, R2.Pin_0, A2.+5V
  N6: S1.Pin_3, S1.Pin_4, A2.~D2

custom parts:
  SSR-40VA: SSR-40VA solid state relay.
  sct-013: sct-013 Current transformer. The pcb footprint is from the 3.5mm stereo jack (as the sensor comes with a 3.5 mm stero plug).
  Arduino MKR Wifi 1010: Arduino MKR Wifi 1010, SAMD21 Cortex-M0+ 32bit Low Power ARM MCU,Flash Memory 256 KB, SRAM 32KB, 48mhz clock, Ublok Wifi interface. V2 Nov 2023 hybrid doesn't work correctly and breaks DRC so remove it.
